# Fritzing sketch circuit_diagram (saved by Fritzing 0.9.3b)

parts:
  Raspberry_Pi_1 = Raspberry Pi 3 [part_number=RPI-3-V1.2]
  U1 = XBee
  CAMERA1 = TTL Serial JPEG Camera  # not connected
  K1 = CO2 sensor [package=PCB]
  Part2 = Adafruit USB DC Solar LiPo Charger [part_number="Adafruit #390"]  # not connected
  Solar_pannel3 = solar_pannel  # not connected
  U3 = LIPO-2000mAh [package=lipo-2000]  # not connected
  Part3 = Adafruit USB DC Solar LiPo Charger [part_number="Adafruit #390"]  # not connected
  U4 = LIPO-2000mAh [package=lipo-2000]  # not connected
  Solar_pannel4 = solar_pannel  # not connected

nets:
  N1: Raspberry_Pi_1.GPIO2, K1.I2C_SDA
  N2: Raspberry_Pi_1.GPIO3, K1.I2C_SCL
  N3: Raspberry_Pi_1.GIPO15, U1.pin2
  N4: Raspberry_Pi_1.GIPO14, U1.pin3

custom parts:
  TTL Serial JPEG Camera: TTL Serial JPEG Camera with NTSC Out
  CO2 sensor: A CO2 sensor from CO2Meter - K30. Datasheet http://co2meters.com/Documentation/Datasheets/DS30-01%20-%20K30.pdf Could not make fine PCB and principal. You should make yours if needed.
  Adafruit USB DC Solar LiPo Charger: Make your projects to go green this summer with our specialized USB/Solar Lithium Ion Polymer Battery charger! This charger is a very unique design, perfect for outdoor projects, or DIY iPod chargers. We've spent over a year testing and tinkering with this charger to come up with a plug and play solution to charging batteries with the sun and we're really pleased with what we ended up with.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
  solar_pannel: Solar pannel
